# Fritzing sketch circuit (saved by Fritzing 0.9.3b)
breadboards: 1

parts:
  Part1 = RFID-RC522
  Part2 = Adafruit Pi Cobbler Plus [part_number="Adafruit #2029"]
  R1 = Resistor [tolerance=±5% resistance=220 package=THT]
  LED1 = LED - 5mm [color="Red (633nm)" package="5 mm [THT]"]

nets:
  N1: Part1.SDA, Part2.CE0
  N2: Part1.SCK, Part2.SCLK
  N3: Part1.MOSI, Part2.MOSI
  N4: Part1.MISO, Part2.MISO
  GND: Part1.GND, Part2.GND, LED1.cathode
  N5: Part1.RST, Part2.GPIO25
  N6: Part1.3_3V, Part2.+3.3V
  N7: Part2.GPIO5, R1.Pin_1
  N8: R1.Pin_0, LED1.anode

custom parts:
  RFID-RC522: The simple China made RFID reader
  Adafruit Pi Cobbler Plus: The Raspberry Pi B+/Pi 2/ Pi 3 has landed on the Maker World like a 40-GPIO pinned, quad-USB ported, credit card sized bomb of DIY joy. And while you can use most of our great Model B accessories by hooking up our downgrade cable, its probably a good time to upgrade your set up and accessorize using all of the Model B+'s / Pi 2's / Pi 3's 40 pins. That's why we now carry the Adafruit Assembled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
